# Fritzing sketch lcd_3pin (saved by Fritzing 0.9.3b)
circuit board: 4.66232cm x 3.84264cm
breadboards: 1

parts:
  U1 = 74HC595 [package="DIP16 [THT]"]
  J2 = Generic rounded female header - 5 pins [form="♀ (female rounded)" package=THT]
  R2 = Resistor [tolerance=±5% resistance=4.7k package=THT]
  LCD1 = LCD screen

nets:
  N1: U1.Q1, LCD1.DB7
  N2: U1.Q2, LCD1.DB6
  N3: U1.Q3, LCD1.DB5
  N4: U1.Q4, LCD1.DB4
  N5: U1.Q7, LCD1.RS
  GND: U1.GND, U1.OE, J2.GND, R2.Pin_0, LCD1.VSS, LCD1.R/W, LCD1.LED-
  VCC: U1.MR, U1.VCC, J2.VCC, LCD1.VDD, LCD1.LED+
  N6: U1.SH_CP, J2.SR_CLOCK
  N7: U1.ST_CP, J2.SR_LATCH
  N8: U1.DS, J2.SR_DATA
  N9: U1.Q0, LCD1.E
  N10: R2.Pin_1, LCD1.V0

custom parts:
  Generic rounded female header - 5 pins: Generic rounded female header
